# Fritzing sketch sketch (saved by Fritzing 0.9.3b)
breadboards: 1

parts:
  WeMos_D1_Mini1 = WeMos D1 Mini
  R3 = Resistor [tolerance=±5% resistance=2.2k package="2512 [SMD]"]  # not connected
  R4 = Resistor [tolerance=±5% resistance=2.2k package="2512 [SMD]"]
  R5 = Resistor [tolerance=±5% resistance=2.2k package="2512 [SMD]"]
  R6 = Resistor [tolerance=±5% resistance=10k package="0603 [SMD]"]
  R1 = Resistor [tolerance=±5% resistance=10k package="0603 [SMD]"]
  R7 = Resistor [tolerance=±5% resistance=10k package="0603 [SMD]"]
  R8 = Resistor [tolerance=±5% resistance=10k package="0603 [SMD]"]
  R2 = Resistor [tolerance=±5% resistance=2.2k package="2512 [SMD]"]  # not connected

nets:
  N1: WeMos_D1_Mini1.G, R6.Pin_0, R1.Pin_1, R7.Pin_1
  N2: R4.Pin_1, R6.Pin_1
  N3: R5.Pin_1, R8.Pin_0

notes:
  12V ground
  12V+ (D1 signal)
  12V+ (D0 signal)
  2K ohm resistors
  10K ohm resistors (pull-down)
